# Fritzing sketch sensorboard (saved by Fritzing 0.9.3b)
breadboards: 1

parts:
  Adafruit_HUZZAH_ESP8266_Breakout1 = Adafruit HUZZAH ESP8266 Breakout [part_number=2471]

nets:
  N1: Adafruit_HUZZAH_ESP8266_Breakout1.#16, Adafruit_HUZZAH_ESP8266_Breakout1.RST
